# Fritzing sketch coverme (saved by Fritzing 0.8.0b)
breadboards: 1

parts:
  Part1 = Arduino Uno (Rev3)
  R1 = Resistor [tolerance=±5% resistance=220 package=THT]
  LED1 = LED - 5mm [color="Red (633nm)" package="5 mm [THT]"]
  LED2 = LED - 5mm [color="Red (633nm)" package="5 mm [THT]"]
  R2 = Resistor [tolerance=±5% resistance=220 package=THT]
  R3 = Photocell (LDR) [package=THT]
  C1 = Electrolytic Capacitor [capacitance=1µF package="100 mil [THT, electrolytic]"]

nets:
  N1: Part1.GND, LED1.cathode, LED2.cathode, C1.-
  N2: Part1.D2, R3.pin_0, C1.+
  N3: Part1.D4, R1.Pin_1
  N4: Part1.D5_PWM, R2.Pin_1
  N5: Part1.5V, R3.pin_1
  N6: R1.Pin_0, LED1.anode
  N7: LED2.anode, R2.Pin_0
